// Digital circuit CTRL_UNIT.dig as structural Verilog
module CTRL_UNIT (
  input  [15:0] INSTR,
  output [2:0] RSA1,
  output [2:0] RSA2,
  output [2:0] RDA,
  output RWE,
  output [2:0] ALOP,
  output OP2Sel,
  output [7:0] RS2Im
);

  wire and_2_out, and_3_out, nor_1_out;

  and and_1 (OP2Sel, ~INSTR[0], INSTR[1]);  // And
  nor nor_1 (nor_1_out, INSTR[0], INSTR[1]);
  Multiplexer #(.Bits(3)) multiplexer_1 (.sel(OP2Sel), .in_0(INSTR[12:10]), .in_1(INSTR[15:13]), .out(RSA1));
  Multiplexer #(.Bits(3)) multiplexer_2 (.sel(OP2Sel), .in_0(INSTR[6:4]), .in_1(INSTR[4:2]), .out(ALOP));
  and and_2 (and_2_out, nor_1_out, INSTR[2], ~INSTR[3]);  // And
  and and_3 (and_3_out, nor_1_out, ~INSTR[2], INSTR[3]);  // And
  or or_1 (RWE, OP2Sel, and_2_out, and_3_out);
  assign RS2Im = OP2Sel ? INSTR[12:5] : 8'bz;  // Driver driver_1
  assign RS2Im = and_3_out ? {3'b000, INSTR[9:5]} : 8'bz;  // Driver driver_2

  assign RDA = INSTR[15:13];
  assign RSA2 = INSTR[9:7];

  // Notes on the sheet:
  //   Decode
  //   Branch Instr.
  //   ALU Imm. Instr.
  //   ALU Instr.
  //   Load Instr.
  //   Select RDA 
  //   as RSA2?
  //   Register Source /
  //   Destination Addresses
  //   2. Operand Select
  //   0 = RS2
  //   1 = Imm.
  //   ALU Operation
  //   Register Destination
  //   Write Enable
  //   Register 2 Immediate
  //   Input
endmodule
